# Fritzing sketch respi_V0 (saved by Fritzing 0.9.4)
breadboards: 1

parts:
  Composant1 = Arduino Uno (Rev3)
  Valve_1_-_input_from_blower = Basic Servo
  valve_2_exchange_box_with_patient = Basic Servo
  pw+ = Pushbutton [package=THT]
  pw- = Pushbutton [package=THT]
  rb+ = Pushbutton [package=THT]
  rb- = Pushbutton [package=THT]
  LCD1 = LCD screen
  R1 = Rotary Potentiometer (Small) [maximum_resistance=10kΩ package=THT]
  pep+ = Pushbutton [package=THT]
  pep- = Pushbutton [package=THT]
  alarme = Piezo Speaker
  U1 = mystery part, 4 pins [chip_label="mpx 10 gp"]
  R2 = Resistor [tolerance=±5% resistance=1M package=THT]
  R3 = Resistor [tolerance=±5% resistance=10k package=THT]
  IC1 = IC, DIP package, 8 pins [chip_label=LM741]

nets:
  N1: Composant1.A0, pw+.leg1
  N2: Composant1.A1, pw-.leg1
  N3: Composant1.A2, rb+.leg1
  N4: Composant1.A3, rb-.leg1
  N5: Composant1.A4/SDA, R2.Pin_1, IC1.pin6
  N6: Composant1.D8, LCD1.E
  N7: Composant1.D9_PWM, LCD1.DB4
  N8: Composant1.D10_PWM/SS, LCD1.DB5
  N9: Composant1.D11_PWM/MOSI, LCD1.DB6
  N10: Composant1.D12/MISO, LCD1.DB7
  GND: Composant1.GND, Valve_1_-_input_from_blower.gnd, valve_2_exchange_box_with_patient.gnd, pw+.leg0, pw-.leg0, rb+.leg0, rb-.leg0, LCD1.VSS, LCD1.R/W, LCD1.LED-, R1.leg2, pep+.leg0, pep-.leg0, alarme.pin2, U1.pin1, R3.Pin_0, IC1.pin4
  N11: Composant1.D2, Valve_1_-_input_from_blower.pulse
  N12: Composant1.D3_PWM, alarme.pin1
  N13: Composant1.D4, valve_2_exchange_box_with_patient.pulse
  N14: Composant1.D5_PWM, pep-.leg1
  N15: Composant1.D6_PWM, pep+.leg1
  N16: Composant1.D7, LCD1.RS
  5V: Composant1.5V, Valve_1_-_input_from_blower.vcc, valve_2_exchange_box_with_patient.vcc, LCD1.VDD, LCD1.LED+, R1.leg1, U1.pin3, IC1.pin7
  N17: LCD1.V0, R1.wiper
  N18: U1.pin2, IC1.pin3
  N19: R2.Pin_0, R3.Pin_1, IC1.pin2
