# Fritzing sketch respi_V0 (saved by Fritzing 0.9.4)
breadboards: 1

parts:
  Composant1 = Arduino Uno (Rev3)
  Valve_1_-_input_from_blower = Basic Servo
  valve_2_exchange_box_with_patient = Basic Servo
  LCD1 = LCD screen
  R1 = Rotary Potentiometer (Small) [maximum_resistance=10kΩ package=THT]
  S1 = Pushbutton [package=THT]
  S2 = Pushbutton [package=THT]
  R2 = Resistor [tolerance=±5% resistance=12k package=THT]
  R3 = Resistor [tolerance=±5% resistance=8.2k package=THT]
  S3 = Pushbutton [package=THT]
  R4 = Resistor [tolerance=±5% resistance=5.6k package=THT]
  S4 = Pushbutton [package=THT]
  R5 = Resistor [tolerance=±5% resistance=3.3k package=THT]
  S5 = Pushbutton [package=THT]
  R6 = Resistor [tolerance=±5% resistance=2.2k package=THT]
  S6 = Pushbutton [package=THT]
  R7 = Resistor [tolerance=±5% resistance=1k package=THT]
  S7 = Pushbutton [package=THT]
  S8 = Pushbutton [package=THT]
  R9 = Resistor [tolerance=±5% resistance=20k package=THT]
  S9 = Pushbutton [package=THT]
  R10 = Resistor [tolerance=±5% resistance=33k package=THT]
  S10 = Pushbutton [package=THT]
  R11 = Resistor [tolerance=±5% resistance=68k package=THT]
  R12 = Resistor [tolerance=±5% resistance=8.2k package=THT]

nets:
  N1: Composant1.A0, R2.Pin_1, R3.Pin_1, R4.Pin_1, R5.Pin_1, R6.Pin_1, R7.Pin_1, S7.leg1, R9.Pin_1, R10.Pin_1, R11.Pin_1, R12.Pin_1
  pressure: Composant1.A1
  niveau bat.: Composant1.A3
  i2c / SCL: Composant1.A5/SCL
  N2: Composant1.D8, LCD1.E
  N3: Composant1.D9_PWM, LCD1.DB4
  N4: Composant1.D10_PWM/SS, LCD1.DB5
  N5: Composant1.D11_PWM/MOSI, LCD1.DB6
  N6: Composant1.D12/MISO, LCD1.DB7
  alarme: Composant1.D13/SCK
  GND: Composant1.GND, Valve_1_-_input_from_blower.gnd, valve_2_exchange_box_with_patient.gnd, LCD1.VSS, LCD1.R/W, LCD1.LED-, R1.leg2, S1.leg0, S2.leg0, S3.leg0, S4.leg0, S5.leg0, S6.leg0, S7.leg0, S8.leg0, S9.leg0, S10.leg0
  AREF: Composant1.AREF
  i2c / SDA: Composant1.A4/SDA
  N7: Composant1.D2, Valve_1_-_input_from_blower.pulse
  N8: Composant1.D4, valve_2_exchange_box_with_patient.pulse
  moteur PWM: Composant1.D5_PWM
  moteur On/off: Composant1.D6_PWM
  N9: Composant1.D7, LCD1.RS
  5V: Composant1.5V, Valve_1_-_input_from_blower.vcc, valve_2_exchange_box_with_patient.vcc, LCD1.VDD, LCD1.LED+, R1.leg1, R12.Pin_0
  N10: LCD1.V0, R1.wiper
  N11: S1.leg1, R2.Pin_0
  N12: S2.leg1, R3.Pin_0
  N13: S3.leg1, R4.Pin_0
  N14: S4.leg1, R5.Pin_0
  N15: S5.leg1, R6.Pin_0
  N16: S6.leg1, R7.Pin_0
  N17: S8.leg1, R9.Pin_0
  N18: S9.leg1, R10.Pin_0
  N19: S10.leg1, R11.Pin_0
